# Fritzing sketch UART-Arduino_RL78_F24 (saved by Fritzing 0.9.3b)
breadboards: 1

parts:
  Part1 = Arduino Nano (Rev3.0)
  JP1 = Header 6 [package=molex-1x6-ra_lock]
  JP2 = Header 6 [package=molex-1x6-ra_lock]

nets:
  N1: Part1.D1/TX, JP1.4
  N2: Part1.GND, JP2.3
  N3: Part1.D3, JP1.3
